// Logisim project cpu.circ as structural Verilog: 1 circuit, main circuit cpu
module cpu (
  input  clk,
  input  [31:0] Instruction,
  input  [31:0] MemReadData,
  output [31:0] MemAddress,
  output [31:0] ProgramCounter,
  output [31:0] ra,
  output [31:0] sp,
  output [31:0] t0,
  output [31:0] t1,
  output [31:0] t2,
  output [31:0] s0,
  output [31:0] s1,
  output [31:0] a0,
  output [3:0] MemWriteMask,
  output [31:0] MemWriteData
);

  wire ASel, BrEq, BrLt, BrUn, BSel, MemRW, PCSel, RegWEn;
  wire [1:0] WBSel;
  wire [2:0] ImmSel;
  wire [3:0] ALUSel;
  wire [31:0] adder_1_out, Cur_Instruction, Cur_ProgramCounter, DataToReg, Immediate, multiplexer_1_out,
       multiplexer_2_out, multiplexer_3_out, multiplexer_4_out, multiplexer_5_out, PCadd4, ReadData1,
       ReadData2;

  Adder #(.width(32)) adder_1 (.a(ProgramCounter), .b(32'h4), .out(adder_1_out));  // open: cin, cout
  Register #(.width(32)) PC (.D(multiplexer_1_out), .clk(clk), .Q(ProgramCounter));  // open: en, clr
  Multiplexer #(.width(32)) multiplexer_1 (.in0(adder_1_out), .in1(MemAddress), .out(multiplexer_1_out), .sel(PCSel));
  Multiplexer #(.width(32)) multiplexer_2 (.in0(Instruction), .in1(32'h13), .out(multiplexer_2_out), .sel(PCSel));
  Multiplexer #(.select(2), .width(32)) multiplexer_3 (
    .in0(DataToReg), .in1(MemAddress), .in2(PCadd4), .out(multiplexer_3_out), .sel(WBSel));  // open: in3
  Register #(.width(32)) register_1 (.D(multiplexer_2_out), .clk(clk), .Q(Cur_Instruction));  // open: en, clr
  Register #(.width(32)) register_2 (.D(ProgramCounter), .clk(clk), .Q(Cur_ProgramCounter));  // open: en, clr
  control_logic control_logic_1 (
    .Instruction(Cur_Instruction), .BrEq(BrEq), .BrLt(BrLt), .PCSel(PCSel), .RegWEn(RegWEn), .ImmSel(ImmSel),
    .BrUn(BrUn), .ASel(ASel), .BSel(BSel), .ALUSel(ALUSel), .MemRW(MemRW), .WBSel(WBSel));
  regfile regfile_1 (
    .ReadIndex1(Cur_Instruction[19:15]), .ReadIndex2(Cur_Instruction[24:20]),
    .WriteIndex(Cur_Instruction[11:7]), .WriteData(multiplexer_3_out), .RegWEn(RegWEn), .clk(clk), .ra(ra),
    .sp(sp), .t0(t0), .t1(t1), .t2(t2), .s0(s0), .s1(s1), .a0(a0), .ReadData1(ReadData1),
    .ReadData2(ReadData2));
  imm_gen imm_gen_1 (.Instruction(Cur_Instruction), .ImmSel(ImmSel), .Immediate(Immediate));
  Adder #(.width(32)) adder_2 (.a(32'h4), .b(Cur_ProgramCounter), .out(PCadd4));  // open: cin, cout
  Multiplexer #(.width(32)) multiplexer_4 (
    .in0(ReadData1), .in1(Cur_ProgramCounter), .out(multiplexer_4_out), .sel(ASel));
  Multiplexer #(.width(32)) multiplexer_5 (.in0(ReadData2), .in1(Immediate), .out(multiplexer_5_out), .sel(BSel));
  alu alu_1 (.A(multiplexer_4_out), .B(multiplexer_5_out), .ALUSel(ALUSel), .ALUResult(MemAddress));
  branch_comp branch_comp_1 (.BrData1(ReadData1), .BrData2(ReadData2), .BrUn(BrUn), .BrEq(BrEq), .BrLt(BrLt));
  partial_store partial_store_1 (
    .Instruction(Cur_Instruction), .MemAddress(MemAddress), .DataFromReg(ReadData2), .MemRW(MemRW),
    .MemWriteMask(MemWriteMask), .DataToMem(MemWriteData));
  partial_load partial_load_1 (
    .Instruction(Cur_Instruction), .MemAddress(MemAddress), .DataFromMem(MemReadData), .DataToReg(DataToReg));

  // Other names for the same wires on the sheet: ALUResult[31:0] = MemAddress

  // Notes on the sheet:
  //   To IMEM
  //   IMEM (do **NOT** move this)
  //   From IMEM
  //   Inputs/Outputs for testing. Do **NOT** move these.
  //   To DMEM
  //   DMEM (do **NOT** move this)
  //   From DMEM
endmodule
