// Logisim project imm-gen.circ as structural Verilog: 1 circuit, main circuit imm_gen
module imm_gen (
  input  [31:0] Instruction,
  input  [2:0] ImmSel,
  output [31:0] Immediate
);

  wire comparator_1_eq, comparator_2_eq;
  wire [31:0] and_1_out, and_2_out, B_type, is_B, is_I;
  wire [31:11] I_type;

  assign I_type = {{20{Instruction[31]}}, Instruction[31]};  // Bit_Extender bit_extender_1
  assign B_type = {{19{Instruction[31]}}, {Instruction[31], Instruction[7], Instruction[30:25], Instruction[11:8], 1'b0}};  // Bit_Extender bit_extender_2
  Comparator #(.width(3)) comparator_1 (.a(ImmSel), .b(3'b000), .eq(comparator_1_eq));  // open: gt, lt
  Comparator #(.width(3)) comparator_2 (.a(ImmSel), .b(3'b010), .eq(comparator_2_eq));  // open: gt, lt
  assign is_I = {{31{comparator_1_eq}}, comparator_1_eq};  // Bit_Extender bit_extender_3
  assign is_B = {{31{comparator_2_eq}}, comparator_2_eq};  // Bit_Extender bit_extender_4
  assign and_1_out = {I_type, Instruction[30:20]} & is_I;  // AND_Gate and_1, 32 bits wide
  assign and_2_out = B_type & is_B;  // AND_Gate and_2, 32 bits wide
  assign Immediate = and_1_out | and_2_out;  // OR_Gate or_1, 32 bits wide

  // Other names for the same wires on the sheet: I_type[10:0] = Instruction[30:20]

  // Notes on the sheet:
  //   INPUTS to your circuit
  //   DON'T CHANGE THE LOCATIONS OF THE INPUTS AND OUTPUTS!
  //   OUTPUT from your circuit
endmodule
