// Logisim project partial-store.circ as structural Verilog: 1 circuit, main circuit partial_store
module partial_store (
  input  [31:0] Instruction,
  input  [31:0] MemAddress,
  input  [31:0] DataFromReg,
  input  MemRW,
  output [3:0] MemWriteMask,
  output [31:0] DataToMem
);

  wire [3:0] multiplexer_3_out;
  wire [31:0] sb_res, sh_res;

  Multiplexer #(.select(2), .width(32)) multiplexer_1 (
    .in0({{24{1'b0}}, DataFromReg[7:0]}), .in1({{16{1'b0}}, DataFromReg[7:0], {8{1'b0}}}),
    .in2({{8{1'b0}}, DataFromReg[7:0], {16{1'b0}}}), .in3({DataFromReg[7:0], {24{1'b0}}}), .out(sb_res),
    .sel(MemAddress[1:0]));
  Multiplexer #(.select(2), .width(32)) multiplexer_2 (
    .in0({{16{1'b0}}, DataFromReg[15:0]}), .in2({DataFromReg[15:0], {16{1'b0}}}), .out(sh_res),
    .sel(MemAddress[1:0]));  // open: in1, in3
  Multiplexer #(.select(5), .width(4)) multiplexer_3 (
    .in0(4'b0001), .in1(4'b0010), .in2(4'b0100), .in3(4'b1000), .in4(4'b0011), .in6(4'b1100), .in8(4'b1111),
    .out(multiplexer_3_out), .sel({Instruction[14:12], MemAddress[1:0]}));  // open: in5, in7, in9, in10, in11, in12, in13, in14, in15, in16, in17, in18, in19, in20, in21, in22, in23, in24, in25, in26, in27, in28, in29, in30, in31
  Multiplexer #(.width(4)) multiplexer_4 (.in0(4'b0000), .in1(multiplexer_3_out), .out(MemWriteMask), .sel(MemRW));
  Multiplexer #(.select(3), .width(32)) multiplexer_5 (
    .in0(sb_res), .in1(sh_res), .in2(DataFromReg), .out(DataToMem), .sel(Instruction[14:12]));  // open: in3, in4, in5, in6, in7

  // Other names for the same wires on the sheet: addr[1:0] = MemAddress[1:0];
  //   flag[4:0] = {Instruction[14:12], MemAddress[1:0]}; func3[2:0] = Instruction[14:12]; sb[7:0] = DataFromReg[7:0];
  //   sb_00[7:0] = DataFromReg[7:0]; sb_01[15:8] = DataFromReg[7:0]; sb_10[23:16] = DataFromReg[7:0];
  //   sb_11[31:24] = DataFromReg[7:0]; sh[15:0] = DataFromReg[15:0]; sh_00[15:0] = DataFromReg[15:0];
  //   sh_10[31:16] = DataFromReg[15:0]; sw_res[31:0] = DataFromReg

  // Notes on the sheet:
  //   INPUTS to your circuit
  //   DON'T CHANGE THE LOCATIONS OF THE INPUTS AND OUTPUTS!
  //   OUTPUT from your circuit
endmodule
